# Fritzing sketch acrylicsign (saved by Fritzing 0.9.3b)
breadboards: 2

parts:
  D1 = Rectifier Diode [package="Melf DO-213 AA [SMD]"]  # not connected
  D2 = Rectifier Diode [package="Melf DO-213 AA [SMD]"]  # not connected
  R1 = Resistor [tolerance=±5% resistance=220 package="0603 [SMD]"]
  Part1 = NeoPixel Stick [part_number=1426]
  BAT1 = BC9VPC [package=bc9vpc]
  J1 = Power Jack [package=power_jack_pth_lock]
  Part2 = Arduino Nano (Rev3.0)
  C7 = Capacitor Polarized [package=cpol-radial-100uf-25v]
  S1 = Toggle Switch [package=THT]

nets:
  N1: R1.Pin_0, Part1.DATAIN
  N2: R1.Pin_1, Part2.D3
  GND: Part1.GND, J1.GND, Part2.GND, C7.+
  +5V: Part1.+5V, Part2.5V
  N3: BAT1.V-, J1.GNDBREAK
  N4: Part2.VIN, S1.COM
  N5: C7.-, S1.L1

custom parts:
  NeoPixel Stick: Make your own little LED strip arrangement with this stick of NeoPixel LEDs. We crammed 8 of the tiny 5050 (5mm x 5mm) smart RGB LEDs onto a PCB with mounting holes and a chainable design. Use only one microcontroller pin to control as many as you can chain together! Each LED is addressable as the driver chip is inside the LED. Each one has ~18mA constant current drive so the color will be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
