# Fritzing sketch emily (saved by Fritzing 0.9.2b)
breadboards: 1

parts:
  Part1 = Arduino Nano (Rev3.0)
  Disp1 = LBT2088AH [part_number=LBT2088AH]
  R1 = Resistor [tolerance=±5% resistance=220 package="2010 [SMD]"]
  R2 = Resistor [tolerance=±5% resistance=220 package="2010 [SMD]"]
  R3 = Resistor [tolerance=±5% resistance=220 package="2010 [SMD]"]
  R4 = Resistor [tolerance=±5% resistance=220 package="2010 [SMD]"]
  R5 = Resistor [tolerance=±5% resistance=220 package="2010 [SMD]"]
  R6 = Resistor [tolerance=±5% resistance=220 package="2010 [SMD]"]
  R7 = Resistor [tolerance=±5% resistance=220 package="2010 [SMD]"]
  R8 = Resistor [tolerance=±5% resistance=220 package="2010 [SMD]"]

nets:
  N1: Part1.D2, Disp1.pin_14
  N2: Part1.D3, Disp1.pin_12
  N3: Part1.D4, Disp1.pin_9
  N4: Part1.D5, R3.Pin_0
  N5: Part1.D6, R2.Pin_0
  N6: Part1.D7, R1.Pin_0
  N7: Part1.D8, Disp1.pin2
  N8: Part1.D9, Disp1.pin1
  N9: Part1.D10, Disp1.pin_5
  N10: Part1.D12/MISO, R6.Pin_1
  N11: Part1.A5, R8.Pin_1
  N12: Part1.A3, R5.Pin_1
  N13: Part1.A2, R4.Pin_1
  N14: Part1.A1, Disp1.pin_8
  N15: Part1.A0, Disp1.pin_7
  N16: Part1.D13/SCK, R7.Pin_1
  N17: Disp1.pin_3, R1.Pin_1
  N18: Disp1.pin_4, R2.Pin_1
  N19: Disp1.pin_6, R3.Pin_1
  N20: Disp1.pin_10, R4.Pin_0
  N21: Disp1.pin_11, R5.Pin_0
  N22: Disp1.pin_13, R8.Pin_0
  N23: Disp1.pin_15, R6.Pin_0
  N24: Disp1.pin_16, R7.Pin_0
