# Fritzing sketch lightbox (saved by Fritzing 0.9.2b)
breadboards: 2

parts:
  C1 = Electrolytic Capacitor [capacitance=100μF package="0807 [SMD, electrolytic]"]
  R1 = Resistor [tolerance=±5% resistance=220 package="0603 [SMD]"]
  Part1 = NeoPixel Stick [part_number=1426]
  J1 = Power Jack [package=power_jack_combo]
  Part2 = Arduino Nano (Rev3.0)
  U2 = POT [package=alps_pot]
  S1 = Square Pushbutton

nets:
  GND: C1.-, Part1.GND, J1.GND, J1.GNDBREAK, Part2.GND, U2.A, S1.leg1
  +5V: C1.+, Part1.+5V, J1.PWR, Part2.VIN
  N1: R1.Pin_0, Part2.D12/MISO
  N2: R1.Pin_1, Part1.DATAIN
  N3: Part2.D3, S1.leg0
  N4: Part2.D11/MOSI, U2.E
  N5: Part2.A0, U2.S

custom parts:
  NeoPixel Stick: Make your own little LED strip arrangement with this stick of NeoPixel LEDs. We crammed 8 of the tiny 5050 (5mm x 5mm) smart RGB LEDs onto a PCB with mounting holes and a chainable design. Use only one microcontroller pin to control as many as you can chain together! Each LED is addressable as the driver chip is inside the LED. Each one has ~18mA constant current drive so the color will be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
