# Fritzing sketch photoresistor_nopcb (saved by Fritzing 0.9.2b)
breadboards: 1

parts:
  R2 = Resistor [tolerance=±5% resistance=220 package=THT]
  R1 = PHOTOCELL [package=photocell-kit]
  Part1 = Arduino Uno (Rev3)
  R3 = Resistor [tolerance=±5% resistance=220 package=THT]
  LED1 = LED - 5mm [color="Red (633nm)" package="5 mm [THT]"]

nets:
  N1: R2.Pin_0, R1.P$1, Part1.A0
  N2: R2.Pin_1, Part1.5V
  N3: R1.P$2, Part1.GND, R3.Pin_1
  N4: Part1.D9_PWM, LED1.anode
  N5: R3.Pin_0, LED1.cathode
