# Fritzing sketch photoresistor_nopcb_led_array_example (saved by Fritzing 0.9.2b)
breadboards: 1

parts:
  R2 = Resistor [tolerance=±5% resistance=220 package=THT]
  R1 = PHOTOCELL [package=photocell-kit]
  Part1 = Arduino Uno (Rev3)
  LED1 = LED - 5mm [color="Red (633nm)" package="5 mm [THT]"]
  R3 = Resistor [tolerance=±5% resistance=220 package=THT]
  R4 = Resistor [tolerance=±5% resistance=220 package=THT]
  R5 = Resistor [tolerance=±5% resistance=220 package=THT]
  LED2 = LED - 5mm [color="Red (633nm)" package="5 mm [THT]"]
  LED3 = LED - 5mm [color="Red (633nm)" package="5 mm [THT]"]
  LED4 = LED - 5mm [color="Red (633nm)" package="5 mm [THT]"]
  LED5 = LED - 5mm [color="Red (633nm)" package="5 mm [THT]"]
  R6 = Resistor [tolerance=±5% resistance=220 package=THT]
  R7 = Resistor [tolerance=±5% resistance=220 package=THT]

nets:
  N1: R2.Pin_0, R1.P$1, Part1.A0
  N2: R2.Pin_1, Part1.5V
  N3: R1.P$2, Part1.GND, R3.Pin_1, R4.Pin_1, R5.Pin_1, R6.Pin_1, R7.Pin_1
  N4: Part1.D9_PWM, LED3.cathode
  N5: Part1.D10_PWM/SS, LED2.cathode
  N6: Part1.D11_PWM/MOSI, LED4.cathode
  N7: Part1.D5_PWM, LED5.cathode
  N8: Part1.D6_PWM, LED1.cathode
  N9: LED1.anode, R4.Pin_0
  N10: R3.Pin_0, LED5.anode
  N11: R5.Pin_0, LED4.anode
  N12: LED2.anode, R7.Pin_0
  N13: LED3.anode, R6.Pin_0
