# Fritzing sketch wiring_diagram (saved by Fritzing 0.9.3b)
breadboards: 1

parts:
  J1 = Piezo Speaker
  Part3 = Arduino Uno (Rev3) - ICSP
  Part4 = Matrix LED de 8x8 basada en MAX7219

nets:
  GND: J1.pin1, Part3.GND, Part4.GND
  N1: J1.pin2, Part3.D6_PWM
  N2: Part3.D2, Part4.DIN
  N3: Part3.D3_PWM, Part4.CS
  N4: Part3.D4, Part4.CLK
  5V: Part3.5V, Part4.VCC

notes:
  The pins may not be exactly the same here. Red goes to Vcc, Green to GND, and Gray to A0. There may be 4 pins on your part. D0 is not used.
  The CLK and CS pins might be different on your part. Make sure CS goes to pin 3 (yellow wire) and CLK goes to pin 4 (white).
  Your part might look different. If it doesn't have polarity, then the orientation doesn't matter.
