# Fritzing sketch program1 (saved by Fritzing 0.9.2b)
breadboards: 1

parts:
  Part2 = Arduino Ethernet Shield (Rev3)
  R1 = Resistor [tolerance=±5% resistance=220 package="2512 [SMD]"]
  LED1 = smd LED [color="Red (633nm)" package="1206 [SMD]"]

nets:
  N1: Part2.GND, R1.Pin_1
  N2: Part2.PWM_D3, LED1.anode
  N3: R1.Pin_0, LED1.cathode
